// Logisim project 8-Bit-ALU.circ as structural Verilog: 6 circuits, main circuit main
module main (
);

  wire and_1_out, clock_1_out, n1_bit_alu_1_carry_out, n1_bit_alu_2_carry_out, n1_bit_alu_3_carry_out,
       n1_bit_alu_4_carry_out, n1_bit_alu_5_carry_out, n1_bit_alu_6_carry_out, n1_bit_alu_7_carry_out,
       n1_bit_alu_8_carry_out, n8_input_multiplexor_1_output, not_1_out, or_1_out, or_2_out, or_3_out;
  wire [2:0] Control_q;
  wire [7:0] n1_bit_alu_1_output, register_1_q, register_2_q;

  Register register_1 (.Q(register_1_q));  // open: D, en, clk, clr
  Register register_2 (.Q(register_2_q));  // open: D, en, clk, clr
  Register #(.width(3)) Control (.Q(Control_q));  // open: D, en, clk, clr
  _1_bit_ALU u_1_bit_alu_1 (
    .A(register_1_q[0]), .B(register_2_q[0]), .Carry_In(1'b0), .Input(Control_q),
    .Output(n1_bit_alu_1_output[0]), .Carry_Out(n1_bit_alu_1_carry_out));
  _1_bit_ALU u_1_bit_alu_2 (
    .A(register_1_q[1]), .B(register_2_q[1]), .Carry_In(n1_bit_alu_1_carry_out), .Input(Control_q),
    .Output(n1_bit_alu_1_output[1]), .Carry_Out(n1_bit_alu_2_carry_out));
  _1_bit_ALU u_1_bit_alu_3 (
    .A(register_1_q[2]), .B(register_2_q[2]), .Carry_In(n1_bit_alu_2_carry_out), .Input(Control_q),
    .Output(n1_bit_alu_1_output[2]), .Carry_Out(n1_bit_alu_3_carry_out));
  _1_bit_ALU u_1_bit_alu_4 (
    .A(register_1_q[3]), .B(register_2_q[3]), .Carry_In(n1_bit_alu_3_carry_out), .Input(Control_q),
    .Output(n1_bit_alu_1_output[3]), .Carry_Out(n1_bit_alu_4_carry_out));
  _1_bit_ALU u_1_bit_alu_5 (
    .A(register_1_q[4]), .B(register_2_q[4]), .Carry_In(n1_bit_alu_4_carry_out), .Input(Control_q),
    .Output(n1_bit_alu_1_output[4]), .Carry_Out(n1_bit_alu_5_carry_out));
  _1_bit_ALU u_1_bit_alu_6 (
    .A(register_1_q[5]), .B(register_2_q[5]), .Carry_In(n1_bit_alu_5_carry_out), .Input(Control_q),
    .Output(n1_bit_alu_1_output[5]), .Carry_Out(n1_bit_alu_6_carry_out));
  _1_bit_ALU u_1_bit_alu_7 (
    .A(register_1_q[6]), .B(register_2_q[6]), .Carry_In(n1_bit_alu_6_carry_out), .Input(Control_q),
    .Output(n1_bit_alu_1_output[6]), .Carry_Out(n1_bit_alu_7_carry_out));
  _1_bit_ALU u_1_bit_alu_8 (
    .A(register_1_q[7]), .B(register_2_q[7]), .Carry_In(n1_bit_alu_7_carry_out), .Input(Control_q),
    .Output(n1_bit_alu_1_output[7]), .Carry_Out(n1_bit_alu_8_carry_out));
  Register register_3 (.D(n1_bit_alu_1_output), .clk(clock_1_out));  // open: en, Q, clr
  Clock clock_1 (.out(clock_1_out));
  _8_Input_Multiplexor u_8_input_multiplexor_1 (
    .A(1'b0), .B(1'b1), .C(1'b0), .D(1'b0), .E(1'b1), .F(1'b1), .G(1'b0), .H(1'b0), .S2(Control_q[2]),
    .S1(Control_q[1]), .S0(Control_q[0]), .Output(n8_input_multiplexor_1_output));
  not not_1 (not_1_out, or_2_out);
  and and_1 (and_1_out, not_1_out, n1_bit_alu_8_carry_out);
  or or_1 (or_1_out, Control_q[0], Control_q[1]);
  or or_2 (or_2_out, or_1_out, Control_q[2]);
  or or_3 (or_3_out, n8_input_multiplexor_1_output, and_1_out);
  LED Error (.in(or_3_out));
endmodule

module adder (
  input  A,
  input  B,
  input  carry_in,
  output carry_out,
  output sum
);

  wire and_1_out, and_2_out, and_3_out, and_4_out, and_5_out, and_6_out, and_7_out, and_8_out, and_9_out,
       and_10_out, and_11_out, not_1_out, not_2_out, not_3_out, or_1_out, or_2_out, or_3_out;

  and and_1 (and_1_out, not_1_out, not_2_out);
  and and_2 (and_2_out, not_1_out, B);
  not not_1 (not_1_out, A);
  not not_2 (not_2_out, B);
  not not_3 (not_3_out, carry_in);
  and and_3 (and_3_out, and_1_out, carry_in);
  and and_4 (and_4_out, and_2_out, not_3_out);
  or or_1 (or_1_out, and_3_out, and_4_out);
  and and_5 (and_5_out, A, B);
  and and_6 (and_6_out, A, not_2_out);
  and and_7 (and_7_out, and_5_out, carry_in);
  and and_8 (and_8_out, and_6_out, not_3_out);
  and and_9 (and_9_out, B, carry_in);
  or or_2 (or_2_out, and_9_out, and_10_out);
  and and_10 (and_10_out, carry_in, A);
  and and_11 (and_11_out, B, A);
  or or_3 (or_3_out, and_7_out, and_8_out);
  or or_4 (carry_out, or_2_out, and_11_out);
  or or_5 (sum, or_3_out, or_1_out);
endmodule

module multiplexor (
  input  Selector,
  input  A,
  input  B,
  output Output
);

  wire and_1_out, and_2_out, not_1_out, not_2_out, not_3_out;

  not not_1 (not_1_out, A);
  not not_2 (not_2_out, B);
  not not_3 (not_3_out, Selector);
  and and_1 (and_1_out, Selector, B);
  and and_2 (and_2_out, A, not_3_out);
  or or_1 (Output, and_1_out, and_2_out);
endmodule

module _1_bit_ALU (
  input  A,
  input  B,
  input  Carry_In,
  input  [2:0] Input,
  output Output,
  output Carry_Out
);

  wire adder_1_sum, and_1_out, not_1_out, not_2_out, or_1_out;

  adder adder_1 (.A(A), .B(B), .carry_in(Carry_In), .carry_out(Carry_Out), .sum(adder_1_sum));
  and and_1 (and_1_out, A, B);
  or or_1 (or_1_out, A, B);
  not not_1 (not_1_out, and_1_out);
  not not_2 (not_2_out, or_1_out);
  _8_Input_Multiplexor u_8_input_multiplexor_1 (
    .A(adder_1_sum), .B(1'b0), .C(and_1_out), .D(or_1_out), .E(1'b0), .F(1'b0), .G(not_1_out), .H(not_2_out),
    .S2(Input[2]), .S1(Input[1]), .S0(Input[0]), .Output(Output));
endmodule

module _8_Input_Multiplexor (
  input  A,
  input  B,
  input  C,
  input  D,
  input  E,
  input  F,
  input  G,
  input  H,
  input  S2,
  input  S1,
  input  S0,
  output Output
);

  wire n4_bit_multiplexor_1_output, n4_bit_multiplexor_2_output;

  _4_bit_Multiplexor u_4_bit_multiplexor_1 (
    .A(A), .B(B), .C(C), .D(D), .S1(S1), .S0(S0), .Output(n4_bit_multiplexor_1_output));
  _4_bit_Multiplexor u_4_bit_multiplexor_2 (
    .A(E), .B(F), .C(G), .D(H), .S1(S1), .S0(S0), .Output(n4_bit_multiplexor_2_output));
  multiplexor multiplexor_1 (
    .A(n4_bit_multiplexor_1_output), .B(n4_bit_multiplexor_2_output), .Selector(S2), .Output(Output));
endmodule

module _4_bit_Multiplexor (
  input  A,
  input  B,
  input  C,
  input  D,
  input  S1,
  input  S0,
  output Output
);

  wire multiplexor_1_output, multiplexor_2_output;

  multiplexor multiplexor_1 (.A(A), .B(B), .Selector(S0), .Output(multiplexor_1_output));
  multiplexor multiplexor_2 (.A(C), .B(D), .Selector(S0), .Output(multiplexor_2_output));
  multiplexor multiplexor_3 (.A(multiplexor_1_output), .B(multiplexor_2_output), .Selector(S1), .Output(Output));
endmodule
