// Logisim project CookieWatcher.circ as structural Verilog: 2 circuits, main circuit main
module main (
);

  wire clock_1_out, cookiewatcher_1_cookies_done, cookiewatcher_1_cookies_ruined,
       cookiewatcher_2_cookies_done, cookiewatcher_2_cookies_ruined, cookiewatcher_3_cookies_done,
       cookiewatcher_3_cookies_ruined, cookiewatcher_4_cookies_done, cookiewatcher_4_cookies_ruined,
       cookiewatcher_5_cookies_done, cookiewatcher_5_cookies_ruined, cookiewatcher_6_cookies_done,
       cookiewatcher_6_cookies_ruined, Start_Batch_1_out, Start_Batch_2_out, Start_Batch_3_out,
       Start_Batch_4_out, Start_Batch_5_out, Start_Batch_6_out;

  Clock clock_1 (.out(clock_1_out));
  Button Start_Batch_1 (.out(Start_Batch_1_out));
  Button Start_Batch_2 (.out(Start_Batch_2_out));
  Button Start_Batch_3 (.out(Start_Batch_3_out));
  Button Start_Batch_4 (.out(Start_Batch_4_out));
  Button Start_Batch_5 (.out(Start_Batch_5_out));
  Button Start_Batch_6 (.out(Start_Batch_6_out));
  LED led_1 (.in(cookiewatcher_1_cookies_ruined));
  CookieWatcher cookiewatcher_1 (
    .Cookie_Handler(Start_Batch_1_out), .ClockInput(clock_1_out),
    .Cookies_Ruined(cookiewatcher_1_cookies_ruined), .Cookies_Done(cookiewatcher_1_cookies_done));
  LED led_2 (.in(cookiewatcher_1_cookies_done));
  LED led_3 (.in(cookiewatcher_2_cookies_ruined));
  CookieWatcher cookiewatcher_2 (
    .Cookie_Handler(Start_Batch_2_out), .ClockInput(clock_1_out),
    .Cookies_Ruined(cookiewatcher_2_cookies_ruined), .Cookies_Done(cookiewatcher_2_cookies_done));
  LED led_4 (.in(cookiewatcher_2_cookies_done));
  LED led_5 (.in(cookiewatcher_3_cookies_ruined));
  CookieWatcher cookiewatcher_3 (
    .Cookie_Handler(Start_Batch_3_out), .ClockInput(clock_1_out),
    .Cookies_Ruined(cookiewatcher_3_cookies_ruined), .Cookies_Done(cookiewatcher_3_cookies_done));
  LED led_6 (.in(cookiewatcher_3_cookies_done));
  LED led_7 (.in(cookiewatcher_4_cookies_ruined));
  CookieWatcher cookiewatcher_4 (
    .Cookie_Handler(Start_Batch_4_out), .ClockInput(clock_1_out),
    .Cookies_Ruined(cookiewatcher_4_cookies_ruined), .Cookies_Done(cookiewatcher_4_cookies_done));
  LED led_8 (.in(cookiewatcher_4_cookies_done));
  LED led_9 (.in(cookiewatcher_5_cookies_ruined));
  CookieWatcher cookiewatcher_5 (
    .Cookie_Handler(Start_Batch_5_out), .ClockInput(clock_1_out),
    .Cookies_Ruined(cookiewatcher_5_cookies_ruined), .Cookies_Done(cookiewatcher_5_cookies_done));
  LED led_10 (.in(cookiewatcher_5_cookies_done));
  LED led_11 (.in(cookiewatcher_6_cookies_ruined));
  CookieWatcher cookiewatcher_6 (
    .Cookie_Handler(Start_Batch_6_out), .ClockInput(clock_1_out),
    .Cookies_Ruined(cookiewatcher_6_cookies_ruined), .Cookies_Done(cookiewatcher_6_cookies_done));
  LED led_12 (.in(cookiewatcher_6_cookies_done));
endmodule

module CookieWatcher (
  input  Cookie_Handler,
  input  ClockInput,
  output Cookies_Ruined,
  output Cookies_Done
);

  wire and_1_out, and_2_out, and_3_out, and_4_out, and_5_out, and_6_out, and_7_out, and_8_out;
  wire [8:0] counter_1_q;

  Counter #(.width(10), .max('h3ff), .ongoal("stay")) counter_1 (
    .Q({Cookies_Done, counter_1_q}), .clk(ClockInput), .clr(Cookie_Handler));  // open: load, D, count, carry
  and and_1 (and_1_out, counter_1_q[0], counter_1_q[1]);
  and and_2 (and_2_out, and_1_out, and_3_out);
  and and_3 (and_3_out, counter_1_q[2], counter_1_q[3]);
  and and_4 (and_4_out, counter_1_q[4], counter_1_q[5]);
  and and_5 (and_5_out, counter_1_q[6], counter_1_q[7]);
  and and_6 (and_6_out, and_5_out, and_7_out);
  and and_7 (and_7_out, counter_1_q[8], Cookies_Done);
  and and_8 (and_8_out, and_2_out, and_4_out);
  and and_9 (Cookies_Ruined, and_8_out, and_6_out);
endmodule
